// Logisim project ejercicio1_c.circ as structural Verilog: 1 circuit, main circuit main
module main (
  input  x,
  input  y,
  input  z,
  output F1,
  output F2
);

  wire AND_21_out, AND_22_out, AND_23_out, AND_24_out, NOT_11_out, NOT_12_out, OR_21_out, XOR_21_out;

  not NOT_11 (NOT_11_out, x);
  xor XOR_21 (XOR_21_out, y, z);
  and AND_21 (AND_21_out, x, OR_21_out);
  or OR_21 (OR_21_out, z, y);
  and AND_22 (AND_22_out, z, y);
  and AND_23 (AND_23_out, x, NOT_12_out);
  not NOT_12 (NOT_12_out, XOR_21_out);
  and AND_24 (AND_24_out, NOT_11_out, XOR_21_out);
  or OR_22 (F1, AND_21_out, AND_22_out);
  or OR_23 (F2, AND_23_out, AND_24_out);
endmodule
