// Logisim project circuito_ej2.circ as structural Verilog: 4 circuits, main circuit Circuito A
module CircuitoB (
  input  [1:0] sin,
  output [6:0] sout1,
  output [6:0] sout2,
  output [6:0] sout3
);

  wire decoder_1_out2;

  Decoder_part #(.select(2)) decoder_1 (
    .out0(sout2[3]), .out1(sout1[5]), .out2(decoder_1_out2), .out3(decoder_1_out2), .sel(sin), .en(1'b1));
  or OR2_3 (sout2[5], sout2[3], sout1[5]);

  assign {sout1[6], sout1[4:0]} = {1'b0, {5{sout1[5]}}};
  assign {sout2[6], sout2[4], sout2[2:0]} = {sout1[5], sout2[5], {2{sout2[3]}}, sout2[5]};
  assign sout3 = {sout2[5], sout1[5], sout2[5], 1'b0, sout2[3], 1'b0, sout1[5]};
endmodule

module Circuito_A (
  input  habilita,
  input  m0,
  input  m1,
  input  m2,
  output [1:0] disp,
  output alarma,
  output vigila
);

  wire AND2_1_out, AND2_2_out, OR2_1_out, XOR2_1_out;

  xor XOR2_1 (XOR2_1_out, m1, m2);
  and AND2_2 (AND2_2_out, m0, XOR2_1_out);
  and AND2_1 (AND2_1_out, m1, m2);
  or OR2_1 (OR2_1_out, AND2_2_out, AND2_1_out);
  nor NOR3_1 (vigila, m0, m1, m2);
  not NOT1_1 (disp[0], habilita);
  and AND2_3 (alarma, habilita, OR2_1_out);

  assign disp[1] = 1'b0;
endmodule

module Decoder (
  input  Enable,
  input  [1:0] Select,
  output _0,
  output _1,
  output _2,
  output _3
);

  wire not_1_out, not_2_out;

  not not_1 (not_1_out, Select[0]);
  not not_2 (not_2_out, Select[1]);
  and and_1 (_0, not_1_out, Enable, not_2_out);
  and and_2 (_1, Select[0], Enable, not_2_out);
  and and_3 (_2, not_1_out, Enable, Select[1]);
  and and_4 (_3, Select[0], Enable, Select[1]);
endmodule

module Main_Ejercicio_2 (
  input  Habilita,
  input  m0,
  input  m1,
  input  m2,
  output Alarma,
  output Vigila
);

  wire [1:0] circuito_a_2_disp;
  wire [6:0] circuitob_1_sout1, circuitob_1_sout2, circuitob_1_sout3;

  Circuito_A circuito_a_1 ();  // open: habilita, m0, m1, m2, disp, alarma, vigila
  Circuito_A circuito_a_2 (
    .habilita(Habilita), .m0(m0), .m1(m0), .m2(m2), .disp(circuito_a_2_disp), .alarma(Alarma), .vigila(Vigila));
  CircuitoB circuitob_1 (
    .sin(circuito_a_2_disp), .sout1(circuitob_1_sout1), .sout2(circuitob_1_sout2), .sout3(circuitob_1_sout3));
  _7_Segment_Display u_7_segment_display_1 (
    .g(circuitob_1_sout1[6]), .f(circuitob_1_sout1[5]), .a(circuitob_1_sout1[0]), .b(circuitob_1_sout1[1]),
    .e(circuitob_1_sout1[4]), .d(circuitob_1_sout1[3]), .c(circuitob_1_sout1[2]), .dp(1'b0));
  _7_Segment_Display u_7_segment_display_2 (
    .g(circuitob_1_sout2[6]), .f(circuitob_1_sout2[5]), .a(circuitob_1_sout2[0]), .b(circuitob_1_sout2[1]),
    .e(circuitob_1_sout2[4]), .d(circuitob_1_sout2[3]), .c(circuitob_1_sout2[2]), .dp(1'b0));
  _7_Segment_Display u_7_segment_display_3 (
    .g(circuitob_1_sout3[6]), .f(circuitob_1_sout3[5]), .a(circuitob_1_sout3[0]), .b(circuitob_1_sout3[1]),
    .e(circuitob_1_sout3[4]), .d(circuitob_1_sout3[3]), .c(circuitob_1_sout3[2]), .dp(1'b0));

  assign m1 = m0;
endmodule
